# Fritzing sketch FINAL PROJECT-FRITZING CAPACITANCE (saved by Fritzing 0.9.3b)
breadboards: 1

parts:
  Part1 = Arduino Mega ADK (Rev3)
  R1 = Resistor [tolerance=±5% resistance=220 package="2010 [SMD]"]
  R2 = Resistor [tolerance=±5% resistance=220 package="2010 [SMD]"]
  C1 = Electrolytic Capacitor [capacitance=1μF package="0405 [SMD, electrolytic]"]

nets:
  N1: Part1.GND, C1.-
  N2: Part1.D13_PWM, R2.Pin_1
  N3: Part1.D11_PWM, R1.Pin_0
  N4: R1.Pin_1, R2.Pin_0, C1.+
