# Fritzing sketch FINAL PROJECT-FRITZING INDUCTANCE  (saved by Fritzing 0.9.3b)
breadboards: 1

parts:
  Part1 = Arduino Mega ADK (Rev3)
  U1 = AD8561 - Ultrafast 7ns Single Supply Comparator [part_number=AD8561]
  C1 = Capacitor [package=cap-pth-small2]
  C2 = Capacitor [package=cap-pth-small2]
  R1 = Resistor [tolerance=±5% resistance=220 package="2010 [SMD]"]
  L1 = Inductor [package="0603 [SMD]"]
  D1 = Diode [package=diode-1n4001]
  R2 = Resistor [tolerance=±5% resistance=220 package="2010 [SMD]"]

nets:
  N1: Part1.A5, U1.+IN, R1.Pin_1
  N2: Part1.D13_PWM, R2.Pin_0
  N3: Part1.D11_PWM, U1.V+, R1.Pin_0, L1.pin_0
  N4: Part1.GND, U1.-IN, U1.OUT, C1.1, C2.1, L1.pin_1
  N5: U1.V-, C1.2, C2.2
  N6: D1.C, R2.Pin_1
