# Fritzing sketch MIDTERM PROJECT-FRITZING DELTA TO WYE (saved by Fritzing 0.9.3b)
breadboards: 1

parts:
  Part1 = Arduino Mega 2560 (Rev3)
  R1 = Resistor [tolerance=±5% resistance=220 package="2010 [SMD]"]
  R2 = Resistor [tolerance=±5% resistance=220 package="2010 [SMD]"]
  R3 = Resistor [tolerance=±5% resistance=220 package="2010 [SMD]"]
  R4 = Resistor [tolerance=±5% resistance=220 package="2010 [SMD]"]

nets:
  N1: Part1.A8, R1.Pin_1, R2.Pin_0
  N2: Part1.A9, R2.Pin_1, R3.Pin_0
  N3: Part1.A10, R3.Pin_1, R4.Pin_0
  N4: Part1.5V, R1.Pin_0
  N5: Part1.GND, R4.Pin_1
